# Fritzing sketch turbid (saved by Fritzing 0.9.3b)
circuit board: 8.46667cm x 5.64444cm
stripboards: 1

parts:
  R1 = Resistor [tolerance=±5% resistance=10k package=THT]
  R5 = Resistor [tolerance=±5% resistance=100 package=THT]
  J1 = male pin header, 4 pins [form="♂ (male)"]
  J2 = male pin header, 4 pins [form="♂ (male)"]
  LED1 = LED - 5mm [color="Red (633nm)" package="5 mm [THT]"]
  J3 = male pin header, 4 pins [form="♂ (male)"]
  Part1 = Arduino Nano (Rev3.0)
  R2 = Resistor [tolerance=±5% resistance=100 package=THT]
  J4 = male alternating pin header, 3 pins [form="♂ (male)"]
  R6 = Resistor [tolerance=±5% resistance=4.7k package=THT]
  C1 = Ceramic Capacitor [capacitance=100nF package="100 mil [THT, multilayer]"]
  C2 = Ceramic Capacitor [capacitance=100nF package="100 mil [THT, multilayer]"]

nets:
  3.3V: R1.Pin_0, Part1.3V3
  N1: R1.Pin_1, J2.pin1, Part1.A0
  N2: R5.Pin_0, Part1.D3
  N3: R5.Pin_1, LED1.anode
  GND: J1.pin1, J2.pin2, J2.pin4, LED1.cathode, J3.pin1, Part1.GND, J4.pin1, C1.0, C2.1
  5V: J1.pin2, J3.pin2, Part1.5V, J4.pin2, R6.Pin_1, C1.1, C2.0
  N4: J1.pin3, Part1.A5
  N5: J1.pin4, Part1.A4
  N6: J2.pin3, R2.Pin_1
  N7: J3.pin3, Part1.D12/MISO
  N8: J3.pin4, Part1.D11/MOSI
  N9: Part1.D2, R2.Pin_0
  N10: Part1.D4, J4.pin3, R6.Pin_0
